# Fritzing sketch distributed_piano (saved by Fritzing 0.9.3b)
breadboards: 1

parts:
  Raspberry_Pi_1 = Raspberry Pi 3 [part_number=RPI-3-V1.2]
  J1 = Piezo Speaker

nets:
  N1: Raspberry_Pi_1.GIPO13, Raspberry_Pi_1.GND, J1.pin1, J1.pin2
